# Fritzing sketch tomadaGenerica (saved by Fritzing 0.6.2b)
breadboards: 1

parts:
  R22 = Resistor [tolerance=±5% resistance=330 package=THT]
  R23 = Resistor [tolerance=±5% resistance=330 package=THT]
  R24 = Resistor [tolerance=±5% resistance=10k package=THT]
  R25 = Resistor [tolerance=±5% resistance=10k package=THT]
  D1 = Rectifier Diode [part_number=1N4001 package="300 mil [THT]"]
  D2 = Rectifier Diode [part_number=1N4001 package="300 mil [THT]"]
  Q1 = npn-Powertransistor [package="TO220 [THT]"]
  Q2 = npn-Powertransistor [package="TO220 [THT]"]
  J14 = female pin header, 1 pin [form="♀ (female)"]
  LED12 = Red LED - 5mm [package="5 mm [THT]"]
  LED13 = Red LED - 5mm [package="5 mm [THT]"]
  J15 = female pin header, 1 pin [form="♀ (female)"]
  J16 = female pin header, 1 pin [form="♀ (female)"]
  J17 = female pin header, 1 pin [form="♀ (female)"]
  J18 = female pin header, 1 pin [form="♀ (female)"]
  J19 = female pin header, 1 pin [form="♀ (female)"]
  J20 = female pin header, 1 pin [form="♀ (female)"]
  J21 = female pin header, 1 pin [form="♀ (female)"]
  J22 = female pin header, 1 pin [form="♀ (female)"]
  J23 = female pin header, 1 pin [form="♀ (female)"]
  J24 = female pin header, 1 pin [form="♀ (female)"]
  J25 = female pin header, 1 pin [form="♀ (female)"]
  J26 = female pin header, 1 pin [form="♀ (female)"]
  J27 = female pin header, 1 pin [form="♀ (female)"]
  J13 = screw terminal, 3 pins
  J28 = screw terminal, 3 pins
  J29 = Screw terminal - 2 pins [package=THT]
  J30 = Screw terminal - 2 pins [package=THT]

nets:
  N1: R22.Pin_0, R23.Pin_1, D1.cathode, D2.cathode, J20.pin1, J27.pin1, J30.pin2
  N2: R22.Pin_1, LED13.anode
  N3: R23.Pin_0, LED12.anode
  N4: R24.Pin_0, J29.pin2
  N5: R24.Pin_1, Q1.base
  N6: R25.Pin_0, Q2.base
  N7: R25.Pin_1, J29.pin1
  N8: D1.anode, Q1.collector, LED13.cathode, J24.pin1
  N9: D2.anode, Q2.collector, LED12.cathode, J21.pin1
  N10: Q1.emitter, Q2.emitter, J30.pin1
  N11: J14.pin1, J22.pin1
  N12: J15.pin1, J13.pin2
  N13: J16.pin1, J28.pin2
  N14: J17.pin1, J23.pin1
  N15: J18.pin1, J13.pin3
  N16: J19.pin1, J13.pin1
  N17: J25.pin1, J28.pin3
  N18: J26.pin1, J28.pin1
